# Fritzing sketch UMC_PWR1310_0321 (saved by Fritzing 0.9.3b)
circuit board: 8.4cm x 8.4cm
breadboards: 1

parts:
  C010 = Ceramic Capacitor [capacitance=100nF package="100 mil [THT, multilayer]"]
  C011 = Ceramic Capacitor [capacitance=100nF package="100 mil [THT, multilayer]"]
  J051 = Header 3 [package=molex-1x3_lock]
  J032 = Header 3 [package=molex-1x3_lock]
  J031 = Header 3 [package=molex-1x3_lock]
  ACS712 = ACS712 Low Current Sensor Board v12
  X031 = screw terminal, 2 pins
  X032 = screw terminal, 2 pins
  DEV-10182 = Monster Moto Shield
  IC010 = Voltage Regulator [package=to-220-alt]
  J061 = female pin header, 3 pins [form="♀ (female)"]
  J060 = female pin header, 3 pins [form="♀ (female)"]
  X010 = screw terminal, 2 pins
  J011 = Header 3 [package=molex-1x3_lock]
  J050 = Header 3 [package=molex-1x3_lock]
  J010 = Header 4 [package=molex-1x4_lock]
  J052 = Header 4 [package=molex-1x4_lock]
  J053 = Header 4 [package=molex-1x4_lock]
  D011 = Diode [part_number=1N4148 package=diode-1n4148]
  D012 = Diode [part_number=1N4148 package=diode-1n4148]
  D010 = Diode [part_number=1N4148 package=diode-1n4148]
  D013 = Diode [part_number=1N4148 package=diode-1n4148]
  D014 = Diode [part_number=1N4148 package=diode-1n4148]
  J012 = Header 3 [package=molex-1x3_lock]
  J071 = female pin header, 3 pins [form="♀ (female)"]
  J070 = female pin header, 3 pins [form="♀ (female)"]
  X011 = screw terminal, 2 pins
  F011 = FUSE [part_number=F2A package=fuse_5mm]
  D001 = Rectifier Diode 10A [part_number=1N5401]
  D002 = Rectifier Diode 10A [part_number=1N5401]
  D003 = Rectifier Diode 10A [part_number=1N5401]
  D004 = Rectifier Diode 10A [part_number=1N5401]
  D005 = Rectifier Diode 10A [part_number=1N5401]

nets:
  GND: C010.0, C011.1, J051.1, J032.1, J031.1, ACS712.GND, DEV-10182.GND, DEV-10182.GND_-_GND@0, DEV-10182.GND_-_GND@1, DEV-10182.GND_-_GND@2, J061.pin1, J060.pin1, X010.pin1, J011.1, J050.1, J010.1, J052.1, J053.1, D013.C, J012.1, J071.pin1, J070.pin1, X011.pin1
  N1: C010.1, ACS712.IP-, DEV-10182.VCC, IC010.IN, D014.C, D001.anode
  7.2V: C011.0, IC010.OUT, J061.pin2, J060.pin2, D014.A
  N2: J051.2, J031.3
  N3: J051.3, J032.3
  5.4V: J032.2, J031.2, ACS712.5V, DEV-10182.5V, J010.2, J071.pin2, J070.pin2
  010: ACS712.IP+, X010.pin2, J010.4
  N4: ACS712.VO, J010.3
  N5: X031.pin1, DEV-10182.OUTA1
  N6: X031.pin2, DEV-10182.OUTB1
  N7: X032.pin1, DEV-10182.OUTA2
  N8: X032.pin2, DEV-10182.OUTB2
  050A: DEV-10182.CS1_-_A2, J050.2
  050B: DEV-10182.CS2_-_A3, J050.3
  052B: DEV-10182.INA2_-_D4, J052.3
  051A: DEV-10182.PWM1_-_D5, J053.2
  052A: DEV-10182.PWM2_-_D6, J052.2
  051B: DEV-10182.INA1_-_D7, J053.3
  051C: DEV-10182.INB1_-_D8, J053.4
  052C: DEV-10182.INB2_-_D9, J052.4
  N9: IC010.GND, D010.A
  N10: J061.pin3, J011.3
  N11: J060.pin3, J011.2
  N12: D011.A, D010.C
  N13: D011.C, D012.A
  N14: D012.C, D013.A
  N15: J012.2, J070.pin3
  N16: J012.3, J071.pin3
  N17: X011.pin2, F011.1
  N18: F011.2, D005.cathode
  N19: D001.cathode, D002.anode
  N20: D002.cathode, D003.anode
  N21: D003.cathode, D004.anode
  N22: D004.cathode, D005.anode

notes:
  BATTERY
  AMC
  AME
  AMB
  MTB
  MTE
  AMT
  MEnSnI
  BlTSnI
  GND
  MEnAhd
  MEnAst
  MEnSpd
  BlTDvn
  BlTEmr
  BlTSpd
  BlTTmp
  MEnTmp
  AMS
  EngBtV
  5.4V
  EngBtI
  AMP
  7.6V
  U-BoatMC, U-Boat Module Controll - Power Shields, 0.321
  PWR
  +
  -
  SNR
  Current Sense
  RD2
  RD1
  Rddr24
  7.2V
  Rddr13
  AMR
  RDD
  M
  UMC_PWR1310 V0.321
  TPB
  TPE
  Rd2Trm
  Rd1Trm
  RP1
  RP2
