# Fritzing sketch UMC_SHD1310_0340 (saved by Fritzing 0.9.2b)
circuit board: 10.1776cm x 5.36194cm
breadboards: 1

parts:
  J553 = Header 4 [package=molex-1x4_lock]
  J554 = Header 4 [package=molex-1x4_lock]
  J555 = Header 4 [package=molex-1x4_lock]
  J454 = Header 3 [package=molex-1x3_lock]
  Q150 = TRANSISTOR_NPN [package=to-92]
  Q140 = TRANSISTOR_NPN [package=to-92]
  Q120 = TRANSISTOR_NPN [package=to-92]
  Q110 = TRANSISTOR_NPN [package=to-92]
  R111 = Resistor [tolerance=±5% resistance=220 package=THT]
  R121 = Resistor [tolerance=±5% resistance=220 package=THT]
  R110 = Resistor [tolerance=±5% resistance=1k package=THT]
  R120 = Resistor [tolerance=±5% resistance=1k package=THT]
  D100 = Rectifier Diode [part_number=1N4007 package="300 mil [THT]"]
  R150 = Resistor [tolerance=±5% resistance=10k package=THT]
  R140 = Resistor [tolerance=±5% resistance=10k package=THT]
  J101 = Header 4 [package=molex-1x4_lock]
  R142 = Resistor [tolerance=±5% resistance=1k package=THT]
  R151 = Resistor [tolerance=±5% resistance=1k package=THT]
  C100 = Ceramic Capacitor [capacitance=100nF package="100 mil [THT, multilayer]"]
  C101 = Ceramic Capacitor [capacitance=100nF package="100 mil [THT, multilayer]"]
  J552 = Header 3 [package=molex-1x3_lock]
  J130 = Header 4 [package=jst-4-pth]
  J132 = Header 2 [package=molex-1x2_lock]
  R101 = Resistor [tolerance=±5% resistance=1k package=THT]
  R102 = Resistor [tolerance=±5% resistance=2.2k package=THT]
  R121_2 = Resistor [tolerance=±5% resistance=1k package=THT]
  R106 = Resistor [tolerance=±5% resistance=2.2k package=THT]
  R105 = Resistor [tolerance=±5% resistance=1k package=THT]
  X100 = screw terminal, 2 pins
  J451 = Header 4 [package=molex-1x4_lock]
  J452 = Header 4 [package=molex-1x4_lock]
  J453 = Header 3 [package=molex-1x3_lock]
  D103 = Rectifier Diode [part_number=1N4007 package="300 mil [THT]"]
  J450 = Header 3 [package=molex-1x3_lock]
  J551 = Header 3 [package=molex-1x3_lock]
  Mega2560_Rev3 = Arduino Mega 2560 (Rev3)
  J133 = Header 2 [package=molex-1x2_lock]
  J556 = Header 4 [package=molex-1x4_lock]
  ICSP1 = female pin header, 3 pins [form="♀ (female)"]  # not connected
  ICSP2 = female pin header, 3 pins [form="♀ (female)"]  # not connected
  J131 = Header 2 [package=molex-1x2_lock]
  J110 = Header 4 [package=jst-4-pth]
  Q130 = TRANSISTOR_NPN [package=to-92]
  R131 = Resistor [tolerance=±5% resistance=220 package=THT]
  R130 = Resistor [tolerance=±5% resistance=1k package=THT]
  S554 = female pin header, 3 pins [form="♀ (female)"]
  D102 = Diode [package=diode-1n4148]
  J455 = Header 3 [package=molex-1x3_lock]
  J550 = female pin header, 3 pins [form="♀ (female)"]
  IC100 = Voltage Regulator [part_number=uA7805 package=to220-igo]

nets (from the pcb view):
  N1: J553.1, J554.1, J555.1, J454.1, Q150.E, Q140.E, Q120.E, Q110.E, J101.1, C100.0, C101.0, J552.1, J130.1, J132.2, R102.Pin_1, R106.Pin_1, X100.pin1, J451.1, J452.1, J453.1, J450.1, J551.1, Mega2560_Rev3.GND, J133.2, J556.1, J131.2, Q130.E, D102.C, J455.1, J550.pin1
  N2: J553.2, J554.2, J555.2, R150.Pin_0, R140.Pin_0, J552.2, Mega2560_Rev3.5V, J556.2
  N3: J553.3, J553.4, Mega2560_Rev3.D22
  N4: J554.3, S554.pin2
  N5: J554.4, Mega2560_Rev3.D26
  N6: J555.3, Mega2560_Rev3.D18/TX1
  N7: J555.4, Mega2560_Rev3.D19/RX1
  N8: J454.2, Mega2560_Rev3.D6_PWM
  N9: J454.3, Mega2560_Rev3.D5_PWM
  N10: Q150.B, R151.Pin_1
  N11: Q150.C, R150.Pin_1, Mega2560_Rev3.RESET
  N12: Q140.B, R142.Pin_0
  N13: Q140.C, R140.Pin_1, Mega2560_Rev3.D42
  N14: Q120.B, R120.Pin_0
  N15: Q120.C, R121.Pin_0
  N16: Q110.B, R110.Pin_0
  N17: Q110.C, R111.Pin_0
  N18: R111.Pin_1, J110.4
  N19: R121.Pin_1, J110.3
  N20: R110.Pin_1, Mega2560_Rev3.D13_PWM
  N21: R120.Pin_1, Mega2560_Rev3.D40
  N22: D100.cathode, C100.1, J132.1, R101.Pin_0, D103.cathode, Mega2560_Rev3.VIN, J110.1, J550.pin3, IC100.IN
  N23: D100.anode, X100.pin2
  N24: J101.2, C101.1, D103.anode, J133.1, J131.1, J550.pin2, IC100.OUT
  N25: J101.3, Mega2560_Rev3.A9
  N26: J101.4, R105.Pin_0
  N27: R142.Pin_1, J130.4
  N28: R151.Pin_0, J130.3
  N29: J552.3, Mega2560_Rev3.A11
  N30: J130.2, R121_2.Pin_1
  N31: R101.Pin_1, R102.Pin_0, Mega2560_Rev3.A12
  N32: R121_2.Pin_0, Mega2560_Rev3.A10
  N33: R106.Pin_0, R105.Pin_1, Mega2560_Rev3.A13
  N34: J451.2, Mega2560_Rev3.D9_PWM
  N35: J451.3, Mega2560_Rev3.D7_PWM
  N36: J451.4, Mega2560_Rev3.D8_PWM
  N37: J452.2, Mega2560_Rev3.D4_PWM
  N38: J452.3, Mega2560_Rev3.D2_PWM
  N39: J452.4, Mega2560_Rev3.D3_PWM
  N40: J453.2, Mega2560_Rev3.A5
  N41: J453.3, Mega2560_Rev3.A6
  N42: J450.2, Mega2560_Rev3.A7
  N43: J450.3, Mega2560_Rev3.A8
  N44: J551.2, Mega2560_Rev3.A14
  N45: J551.3, Mega2560_Rev3.A15
  N46: Mega2560_Rev3.A2, J455.3
  N47: Mega2560_Rev3.A3, J455.2
  N48: Mega2560_Rev3.A4, S554.pin1
  N49: Mega2560_Rev3.D21/SCL, Mega2560_Rev3.SCL, J556.4
  N50: Mega2560_Rev3.D20/SDA, Mega2560_Rev3.SDA, J556.3
  N51: Mega2560_Rev3.D24, S554.pin3
  N52: Mega2560_Rev3.D44, R130.Pin_1
  N53: J110.2, R131.Pin_1
  N54: Q130.B, R130.Pin_0
  N55: Q130.C, R131.Pin_0
  N56: D102.A, IC100.GND

notes:
  GPS
  BTK
  TMP
  PRS
  AMR
  CMP
  AMB
  AME
  AMC
  RPI
  SWT
  AMT
  GND
  MEnSnI
  BlTSnI
  MEnSpd
  MEnAhd
  MEnAst
  BlTEmr
  BlTDvn
  BlTSpd
  MEnTmp
  BlTTmp
  Rddr13
  Rddr24
  LSG
  U-BoatMC, U-Boat Module Controll - Main Shields, 0.340
  7.2V
  RPiBtV
  InoRESET
  RPiGIO
  5.4V
  AMS
  EngBtV
  5V
  EngBtI
  PrsVal
  AMP
  HdwBtV
  NavLgt
  SgFlsh
  TmpExt
  TmpH2O
  BlTFll
  BlTEpt
  RX
  TX
  SonarB
  SonarF
  SNR
  4x
  5x
  1x
  AUX
  RTR
  SCL
  SDA
  RDD
  CURRENT
  ENGINE
  BALLAST TANK
  TEMPERATURE
  RUDDERS
  M
  UMC_SHD1310 V0.340
  SgLink
  A
  D
  C
  Rd2Trm
  Rd1Trm
  RUDDERS POSITION
